# Fritzing sketch gas-detect-robot-circuit-diagram (saved by Fritzing 0.9.3b)
perfboards: 2

parts:
  Raspberry_Pi_1 = Raspberry Pi 3 [part_number=RPI-3-V1.2]
  hc-sr1 = hc-sr04
  hc-sr2 = hc-sr04
  hc-sr3 = hc-sr04
  U1 = LIPO-2000mAh [package=lipo-2000]
  U2 = GAS_SENSOR [package=mq-3]
  M1 = DC Motor
  M2 = DC Motor
  M4 = DC Motor
  U3 = LM2596 step down module
  M5 = DC Motor
  L298N2 = L298N DC motor driver

nets:
  N1: Raspberry_Pi_1.GIPO27, hc-sr2.Echo
  N2: Raspberry_Pi_1.GIPO22, hc-sr2.Trig
  N3: Raspberry_Pi_1.GIPO5, hc-sr3.Trig
  N4: Raspberry_Pi_1.GIPO6, hc-sr3.Echo
  N5: Raspberry_Pi_1.GIPO13, L298N2.IN3
  N6: Raspberry_Pi_1.GIPO19, L298N2.IN4
  N7: Raspberry_Pi_1.GIPO26, U2.B1
  N8: Raspberry_Pi_1.GIPO16, L298N2.IN2
  N9: Raspberry_Pi_1.GND, L298N2.IN1
  N10: Raspberry_Pi_1.GIPO24, hc-sr1.Echo
  N11: Raspberry_Pi_1.GIPO23, hc-sr1.Trig
  VCC: hc-sr1.VCC, hc-sr2.VCC, hc-sr3.VCC
  GND: hc-sr1.GND, hc-sr2.GND, hc-sr3.GND, U2.A1
  N12: U1.+, U3.IN+
  N13: U1.-, U3.IN-, U3.OUT-
  N14: M1.pin_1, M2.pin_1, L298N2.OUT4
  N15: M1.pin_2, M2.pin_2, L298N2.OUT3
  N16: M4.pin_1, M5.pin_1, L298N2.OUT2
  N17: M4.pin_2, M5.pin_2, L298N2.OUT1

notes:
  Raspberry Pi 3
  Battery
  2 x 18650 pin
  3.7 V
  3000 mAh
  Ultrasonic sensor HC-04
  Right Sensor
  Ultrasonic sensor HC-04
  Left Sensor
  Front Sensor HC-04
  Module L298N
  Module LM2596
  Gas Sensor MQ2
  DC motor
  7.4V
  5V

custom parts:
  LM2596 step down module: LM2596 DC-DC step down power supply module 3 A.
  L298N DC motor driver: 2x DC motor driver with 78M05 positive voltage regulator (7..35 V) L298N: max 46 V, 2 A Set 5 V Enable jumper to enable 5 V regultor (needed for the L298N) and +5 V output at screw terminal or supply external +5 V at screw terminal Set ENA and/or ENB to +5 V to enable motor permanently or supply ENA and/or ENB with PWM signal IN1 and IN2 set rotation directory for motor A (OUT1/OUT2) IN2 and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
